# Fritzing sketch Circuit_DHT11_Photocell (saved by Fritzing 0.9.2b)
breadboards: 1

parts:
  Raspberry_Pi1 = Raspberry Pi 2
  RHT1 = Humidity and Temperature Sensor RHT03
  R1 = Resistor [tolerance=±5% resistance=220 package="2010 [SMD]"]
  R2 = PHOTOCELL [package=photocell-kit]
  C2 = Capacitor Polarized [package=cpol-radial-10uf-25v]

nets:
  3V3: Raspberry_Pi1.3v3, RHT1.Vcc, R1.Pin_0, R2.P$1
  N1: Raspberry_Pi1.GPIO4, RHT1.Data-signal, R1.Pin_1
  N2: Raspberry_Pi1.GPIO17, R2.P$2, C2.-
  N3: Raspberry_Pi1.GND, RHT1.GND_2, C2.+
