# Fritzing sketch Circuit_DHT11_TSL2561 (saved by Fritzing 0.9.2b)
breadboards: 1

parts:
  Raspberry_Pi1 = Raspberry Pi 2
  R1 = Resistor [tolerance=±5% resistance=220 package="2010 [SMD]"]
  U2 = SI1120 [package=odfn]
  DHT1 = DHT11 Humitidy and Temperature Sensor

nets:
  N1: Raspberry_Pi1.3v3, U2.TXO, DHT1.DATA
  N2: Raspberry_Pi1.GPIO2, U2.STX
  N3: Raspberry_Pi1.GPIO3, U2.VDD
  N4: Raspberry_Pi1.GPIO4, R1.Pin_1, DHT1.VDD
  GND: Raspberry_Pi1.GND, U2.TXGD, DHT1.GND

custom parts:
  DHT11 Humitidy and Temperature Sensor: DHT11 Humidity and Temperature Sensor
