# Fritzing sketch Circuit_automation (saved by Fritzing 0.9.2b)
breadboards: 2

parts:
  Raspberry_Pi1 = Raspberry Pi 2
  R1 = Resistor [tolerance=±5% resistance=220 package="2010 [SMD]"]
  U2 = SI1120 [package=odfn]
  DHT1 = DHT11 Humitidy and Temperature Sensor
  Q1 = TIP120 Hi-Current Darlington Transistor
  Q2 = TIP120 Hi-Current Darlington Transistor
  R2 = Resistor [tolerance=±5% resistance=1.2k package="2010 [SMD]"]
  R3 = Resistor [tolerance=±5% resistance=1.2k package="2010 [SMD]"]
  D1 = Rectifier Diode [part_number=1N4001 package="Melf DO-213 AB [SMD]"]
  D2 = Rectifier Diode [part_number=1N4001 package="Melf DO-213 AB [SMD]"]
  VCC1 = 4 x AAA Battery Mount
  LED2 = LEDs [package=led10mm]
  LED3 = LEDs [package=led10mm]
  LED4 = LEDs [package=led10mm]
  LED1 = LEDs [package=led10mm]
  LED5 = LEDs [package=led10mm]
  R4 = Resistor [tolerance=±5% resistance=39 package="2010 [SMD]"]
  R5 = Resistor [tolerance=±5% resistance=39 package="2010 [SMD]"]
  R6 = Resistor [tolerance=±5% resistance=39 package="2010 [SMD]"]
  R7 = Resistor [tolerance=±5% resistance=39 package="2010 [SMD]"]
  R8 = Resistor [tolerance=±5% resistance=39 package="2010 [SMD]"]
  R9 = Resistor [tolerance=±5% resistance=39 package="2010 [SMD]"]
  LED6 = LEDs [package=led10mm]
  M1 = DC Motor
  NEOPIXEL1 = Neopixel Strip -- White (30/m)

nets:
  N1: Raspberry_Pi1.3v3, U2.TXO, DHT1.DATA
  N2: Raspberry_Pi1.GPIO2, U2.STX
  N3: Raspberry_Pi1.GPIO3, U2.VDD
  N4: Raspberry_Pi1.GPIO4, R1.Pin_1, DHT1.VDD
  GND: Raspberry_Pi1.GND, U2.TXGD, DHT1.GND, Q1.EMITTER, Q2.EMITTER, D1.anode, D2.anode, VCC1.-
  N5: Raspberry_Pi1.GPIO6, R2.Pin_0
  N6: Raspberry_Pi1.GPIO13, R3.Pin_0
  N7: Q1.BASE, R2.Pin_1
  N8: Q1.COLLECTOR, D1.cathode, R4.Pin_0, R5.Pin_0, R6.Pin_0, R7.Pin_0, R8.Pin_0, R9.Pin_0, NEOPIXEL1.GND
  N9: Q2.BASE, R3.Pin_1
  N10: Q2.COLLECTOR, D2.cathode, M1.pin_1
  N11: VCC1.+, LED2.C, LED3.C, LED4.C, LED1.C, LED5.C, LED6.C, M1.pin_2, NEOPIXEL1.+5V
  N12: LED2.A, R7.Pin_1
  N13: LED3.A, R8.Pin_1
  N14: LED4.A, R6.Pin_1
  N15: LED1.A, R5.Pin_1
  N16: LED5.A, R4.Pin_1
  N17: R9.Pin_1, LED6.A

custom parts:
  DHT11 Humitidy and Temperature Sensor: DHT11 Humidity and Temperature Sensor
  Neopixel Strip -- White (30/m): These NeoPixel strips have 30 digitally-addressable pixel LEDs per meter and are very affordable and are only 12.5 mm wide, 10 mm if you remove the strip from the casing.
