# Fritzing sketch Task3 (saved by Fritzing 0.9.2b)
breadboards: 1

parts:
  LED1 = LED - 5mm [color="Green (565nm)" package="5 mm [THT]"]
  LED2 = LED - 5mm [color="Red (633nm)" package="5 mm [THT]"]
  R1 = Resistor [tolerance=±5% resistance=220 package=THT]
  R2 = Resistor [tolerance=±5% resistance=220 package=THT]
  Raspberry_Pi2 = Raspberry Pi B+
  U2 = POT [package=alps_pot]
  IC1 = IC, DIP package, 8 pins [chip_label=TLC549]

nets:
  N1: LED1.cathode, Raspberry_Pi2.GND, U2.A, IC1.pin3, IC1.pin4
  N2: LED1.anode, R2.Pin_0, Raspberry_Pi2.GPIO27
  N3: LED2.anode, R1.Pin_0, Raspberry_Pi2.GPIO17
  N4: R1.Pin_1, R2.Pin_1, Raspberry_Pi2.3v3, U2.E, IC1.pin1, IC1.pin8
  N5: Raspberry_Pi2.GPIO9, IC1.pin6
  N6: Raspberry_Pi2.GPIO11, IC1.pin7
  N7: Raspberry_Pi2.GPIO8, IC1.pin5
  N8: U2.S, IC1.pin2
